# Fritzing sketch RaspberrypiProject.fzpz (saved by Fritzing 0.9.3b)
breadboards: 1

parts:
  Raspberry_Pi_1 = Raspberry Pi 4 [part_number=RPI-4-b]
  RHT1 = Humidity and Temperature Sensor RHT03
  元件1 = Breakout Board for Electret Microphone
  Lhi1 = LHi958 [package=to-39]
  LED1 = LEDs [package=led10mm]
  R1 = Resistor [tolerance=±5% resistance=220 package=THT]
  IC1 = IC, DIP package, 4 pins [chip_label="Infrared body detector"]

nets:
  VCC: Raspberry_Pi_1.3v3, RHT1.Vcc, 元件1.VCC, Lhi1.n.a., IC1.pin1
  N1: Raspberry_Pi_1.GPIO2, IC1.pin2
  N2: Raspberry_Pi_1.GPIO3, IC1.pin3
  GND: Raspberry_Pi_1.GND, RHT1.GND_1, RHT1.GND_2, 元件1.GND, Lhi1.GND, LED1.A, IC1.pin4
  N3: Raspberry_Pi_1.GPIO13, RHT1.Data-signal
  N4: Raspberry_Pi_1.GPIO19, Lhi1.D
  N5: Raspberry_Pi_1.GPIO26, 元件1.AUD
  N6: Raspberry_Pi_1.GPIO16, R1.Pin_0
  N7: LED1.C, R1.Pin_1

custom parts:
  Raspberry Pi 4: The RPi4, a faster version of the awesome Raspberry Pi 2 B ARM Board with 40 pin gpio. Ready for special Raspberry Pi B+ and RPi2 Hat (Hardware attached (on) top)
